// Logisim project uc.circ as structural Verilog: 4 circuits, main circuit main
module main (
  input  Clock,
  input  Senzor1,
  input  Senzor2,
  input  Reset,
  output Iesire
);

  wire and_1_out, and_2_out, and_3_out, and_4_out, and_5_out, and_6_out, and_7_out, d_ff_1_q, nor_1_out,
       nor_2_out, or_1_out, register_1_q, register_2_q, register_3_q, register_4_q, register_5_q;

  nor nor_1 (nor_1_out, Senzor1, Senzor2);
  and and_1 (and_1_out, Senzor1, ~Senzor2);  // AND_Gate
  and and_2 (and_2_out, Senzor1, Senzor2);
  and and_3 (and_3_out, ~Senzor1, Senzor2);  // AND_Gate
  nor nor_2 (nor_2_out, Senzor1, Senzor2);
  and and_4 (and_4_out, register_1_q, and_1_out);
  and and_5 (and_5_out, register_2_q, and_2_out);
  and and_6 (and_6_out, register_3_q, and_3_out);
  and and_7 (and_7_out, register_4_q, nor_2_out);
  Register #(.width(1)) register_1 (.D(nor_1_out), .en(nor_1_out), .Q(register_1_q), .clk(Clock), .clr(or_1_out));
  Register #(.width(1)) register_2 (.D(and_1_out), .en(and_4_out), .Q(register_2_q), .clk(Clock), .clr(or_1_out));
  Register #(.width(1)) register_3 (.D(and_2_out), .en(and_5_out), .Q(register_3_q), .clk(Clock), .clr(or_1_out));
  Register #(.width(1)) register_4 (.D(and_3_out), .en(and_6_out), .Q(register_4_q), .clk(Clock), .clr(or_1_out));
  Register #(.width(1)) register_5 (.D(nor_2_out), .en(and_7_out), .Q(register_5_q), .clk(Clock), .clr(or_1_out));
  Register #(.width(1)) register_6 (.D(register_5_q), .en(register_5_q), .Q(Iesire), .clk(Clock), .clr(or_1_out));
  D_Flip_Flop d_ff_1 (.clk(Clock), .D(Iesire), .Q(d_ff_1_q));  // open: Qn, preset, en, reset
  or or_1 (or_1_out, Reset, d_ff_1_q);

  // Notes on the sheet:
  //   nor1
  //   and2
  //   and4
  //   and6
  //   nor2
  //   and1
  //   and3
  //   and5
  //   and7
  //   reg1
  //   reg2
  //   reg3
  //   reg4
  //   reg5
  //   reg6
  //   d1
  //   or1
endmodule

module ordsenzori (
  input  Clock,
  input  Senzor1,
  input  Senzor2,
  input  [7:0] Afisor_Fortat,
  input  Senzor3,
  input  Senzor4,
  input  Senzor5,
  input  Senzor6,
  input  Senzor7,
  input  Senzor8,
  input  Reset,
  output Intrare1,
  output [7:0] Afisor,
  output Iesire1,
  output Intrare2,
  output Iesire2
);

  wire d_ff_1_q, d_ff_2_q, demultiplexer_1_out1, demultiplexer_1_out2, demultiplexer_1_out3,
       demultiplexer_2_out1, demultiplexer_2_out2, demultiplexer_2_out3, demultiplexer_3_out1,
       demultiplexer_3_out2, or_3_out, or_4_out;
  wire [1:0] or_1_out;

  main main_1 (.Clock(Clock), .Senzor2(Senzor2), .Iesire(Intrare1), .Senzor1(Senzor1), .Reset(Reset));
  main main_2 (.Clock(Clock), .Senzor2(Senzor4), .Iesire(Iesire1), .Senzor1(Senzor3), .Reset(Reset));
  main main_3 (.Clock(Clock), .Senzor2(Senzor6), .Iesire(Intrare2), .Senzor1(Senzor5), .Reset(Reset));
  main main_4 (.Clock(Clock), .Senzor2(Senzor8), .Iesire(Iesire2), .Senzor1(Senzor7), .Reset(Reset));
  Demultiplexer #(.select(2)) demultiplexer_1 (
    .out1(demultiplexer_1_out1), .out2(demultiplexer_1_out2), .out3(demultiplexer_1_out3), .in(1'b1),
    .sel({Iesire2, Iesire1}));  // open: out0, en
  Demultiplexer #(.select(2)) demultiplexer_2 (
    .out1(demultiplexer_2_out1), .out2(demultiplexer_2_out2), .out3(demultiplexer_2_out3), .in(1'b1),
    .sel({Intrare2, Intrare1}));  // open: out0, en
  D_Flip_Flop d_ff_1 (.clk(Clock), .D(demultiplexer_1_out3), .Q(d_ff_1_q), .reset(Reset));  // open: Qn, preset, en
  D_Flip_Flop d_ff_2 (.clk(Clock), .D(demultiplexer_2_out3), .Q(d_ff_2_q), .reset(Reset));  // open: Qn, preset, en
  or or_1 (or_1_out[0], demultiplexer_1_out1, demultiplexer_1_out2, demultiplexer_1_out3, d_ff_1_q);
  or or_2 (or_1_out[1], demultiplexer_2_out1, demultiplexer_2_out2, demultiplexer_2_out3, d_ff_2_q);
  Demultiplexer #(.select(2)) demultiplexer_3 (
    .out1(demultiplexer_3_out1), .out2(demultiplexer_3_out2), .in(1'b1), .sel(or_1_out));  // open: out0, out3, en
  or or_3 (or_3_out, demultiplexer_3_out1, demultiplexer_3_out2);
  Counter counter_1 (
    .load(or_4_out), .D(Afisor_Fortat), .count(or_3_out), .Q(Afisor), .clk(Clock));  // open: carry, clr
  or or_4 (or_4_out, demultiplexer_3_out2, Reset);

  // Notes on the sheet:
  //   Intrarea_1
  //   Iesirea_1
  //   Intrarea_2
  //   Iesirea_2
  //   dmux1
  //   dmux2
  //   d1
  //   d2
  //   or1
  //   or2
  //   dmux3
  //   or3
  //   num1
  //   or4
endmodule

module proiect_final (
  input  Senzor1,
  input  Senzor2,
  input  Reset,
  input  Senzor3,
  input  Senzor4,
  input  Senzor5,
  input  Senzor6,
  input  Senzor7,
  input  Senzor8,
  input  [7:0] Afisor_Fortat
);

  wire clock_1_out, ordsenzori_1_iesire1, ordsenzori_1_iesire2, ordsenzori_1_intrare1, ordsenzori_1_intrare2;
  wire [7:0] ordsenzori_1_afisor;

  uc uc_1 (.Reset(Reset));
  Clock clock_1 (.out(clock_1_out));
  ordsenzori ordsenzori_1 (
    .Senzor1(Senzor1), .Senzor2(Senzor2), .Senzor3(Senzor3), .Senzor4(Senzor4), .Senzor5(Senzor5),
    .Senzor6(Senzor6), .Senzor7(Senzor7), .Senzor8(Senzor8), .Intrare1(ordsenzori_1_intrare1),
    .Iesire1(ordsenzori_1_iesire1), .Intrare2(ordsenzori_1_intrare2), .Iesire2(ordsenzori_1_iesire2),
    .Reset(Reset), .Afisor(ordsenzori_1_afisor), .Clock(clock_1_out), .Afisor_Fortat(Afisor_Fortat));
  LED Intrarea1 (.in(ordsenzori_1_intrare1));
  LED Iesirea1 (.in(ordsenzori_1_iesire1));
  LED Intrarea2 (.in(ordsenzori_1_intrare2));
  LED Iesirea2 (.in(ordsenzori_1_iesire2));
  Hex_Digit_Display hex_digit_display_1 (.value(ordsenzori_1_afisor[7:4]));  // open: dp
  Hex_Digit_Display hex_digit_display_2 (.value(ordsenzori_1_afisor[3:0]));  // open: dp

  // Notes on the sheet:
  //   UC
  //   UE
endmodule

module uc (
  input  Reset
);
endmodule
